# Fritzing sketch Untitled Sketch (saved by Fritzing 0.9.3b)
breadboards: 1

parts:
  Componente2 = Arduino Uno (Rev3)
  S1 = Pushbutton [package="[THT]"]
  R1 = Resistor [tolerance=±5% resistance=220 package=THT]
  KY-1 = Keyes Relay [package=THT]
  KY-2 = Keyes Relay [package=THT]
  Componente3 = FC-28 Soil Hygrometer Module

nets:
  N1: Componente2.A1, Componente3.AO
  N2: Componente2.D8, S1.Pin_3, S1.Pin_4
  N3: Componente2.GND, R1.Pin_1, KY-1.ground, KY-2.ground
  N4: Componente2.D2, KY-1.signal
  N5: Componente2.D3_PWM, KY-2.signal
  N6: Componente2.D6_PWM, Componente3.GND
  N7: Componente2.D7, Componente3.VCC
  N8: Componente2.5V, KY-1.power, KY-2.power
  N9: S1.Pin_1, S1.Pin_2, R1.Pin_0

notes:
  Sensor umidade do solo
  Rele bomba
  Rele solenoide
  Boia
  PIN 6 = SMS_GND
  PIN 7 = SMS_VCC

custom parts:
  Keyes Relay: The Keyes 5V relay module is suitable for SCM development, home appliance control. It uses a 5V~12V TIL control signal which can control DC / AC signal.
  FC-28 Soil Hygrometer Module: The FC-28 is a soil hygrometer module that uses the Texas Instruments LM393 comparator chip to provide an analog measurement of soil humidity. The digital output is high when soil moisture is over a certain threshold, as determined by adjusting the potentiometer.
